// Logisim project CMFB-16.circ as structural Verilog: 4 circuits, main circuit CPU
module CPU (
);

  wire ALUSrc, button_2_out, button_3_out, C, Clock, GT, JE, JE0, JE1, JE2, JE3, MV, N, V, Z;
  wire [3:0] AluOp;
  wire [15:0] adaptedalu_1_lowoutput, InmediateData, multiplexer_1_out, programcounter_1_counter,
       registers_1_aoutput, registers_1_boutput, WData;
  wire [63:16] Order;

  Button button_1 (.out(Clock));
  Button button_2 (.out(button_2_out));
  ROM #(.addrWidth(16), .dataWidth(64)) rom_1 (
    .addr(programcounter_1_counter),
    .data({Order[63:43], ALUSrc, Order[41], AluOp, JE0, Order[35:16], InmediateData}));
  programCounter programcounter_1 (
    .NumberInput(InmediateData), .DirectNumber(JE), .RunCycle(Clock), .Reset(button_2_out),
    .Counter(programcounter_1_counter));
  LED led_1 (.in(Order[20]));
  LED led_2 (.in(Order[24]));
  LED led_3 (.in(Order[21]));
  LED led_4 (.in(Order[25]));
  LED led_5 (.in(Order[22]));
  LED led_6 (.in(Order[26]));
  LED led_7 (.in(Order[23]));
  LED led_8 (.in(Order[27]));
  LED led_9 (.in(Order[16]));
  LED led_10 (.in(Order[17]));
  LED led_11 (.in(Order[18]));
  LED led_12 (.in(Order[19]));
  LED led_13 (.in(InmediateData[0]));
  LED led_14 (.in(InmediateData[1]));
  LED led_15 (.in(InmediateData[2]));
  LED led_16 (.in(InmediateData[3]));
  LED led_17 (.in(InmediateData[4]));
  LED led_18 (.in(InmediateData[5]));
  LED led_19 (.in(InmediateData[6]));
  LED led_20 (.in(InmediateData[7]));
  LED led_21 (.in(InmediateData[8]));
  LED led_22 (.in(InmediateData[9]));
  LED led_23 (.in(InmediateData[10]));
  LED led_24 (.in(InmediateData[11]));
  LED led_25 (.in(InmediateData[12]));
  LED led_26 (.in(InmediateData[13]));
  LED led_27 (.in(InmediateData[14]));
  LED led_28 (.in(InmediateData[15]));
  Button button_3 (.out(button_3_out));
  and and_1 (JE3, N, Order[33]);
  and and_2 (JE2, Z, Order[34]);
  registers registers_1 (
    .Clock(Clock), .WData(WData), .Reset(button_3_out), .WE(Order[41]), .WAddr(Order[19:16]),
    .RAddrA(Order[23:20]), .RAddrB(Order[27:24]), .AOutput(registers_1_aoutput), .BOutput(registers_1_boutput));
  and and_3 (JE1, GT, Order[35]);
  or or_1 (JE, JE3, JE2, JE1, JE0);
  Multiplexer #(.width(16)) multiplexer_1 (
    .in0(registers_1_boutput), .in1(InmediateData), .out(multiplexer_1_out), .sel(ALUSrc));
  adaptedALU adaptedalu_1 (
    .AInput(registers_1_aoutput), .BInput(multiplexer_1_out), .ControlInput(AluOp), .Clock(Clock),
    .FlagsRegister({Z, MV, N, V, C, GT}), .LowOutput(adaptedalu_1_lowoutput));  // open: Cin, HighOutput
  Multiplexer #(.width(16)) multiplexer_2 (
    .in0(adaptedalu_1_lowoutput), .in1(InmediateData), .out(WData), .sel(Order[43]));

  // Other names for the same wires on the sheet: Order (some bits) = {ALUSrc, AluOp, JE0, InmediateData};
  //   WAddr[3:0] = Order[19:16]; RAddrA[3:0] = Order[23:20]; RAddrB[3:0] = Order[27:24]; WE = Order[41];
  //   ResultSrc = Order[43]
endmodule

module programCounter (
  input  [15:0] NumberInput,
  input  DirectNumber,
  input  RunCycle,
  input  Reset,
  output [15:0] Counter
);

  wire not_1_out;
  wire [1:0] minihalfadder_1_dataoutput, minihalfadder_2_dataoutput, minihalfadder_3_dataoutput,
       minihalfadder_4_dataoutput, minihalfadder_5_dataoutput, minihalfadder_6_dataoutput,
       minihalfadder_7_dataoutput, minihalfadder_8_dataoutput, minihalfadder_9_dataoutput,
       minihalfadder_10_dataoutput, minihalfadder_11_dataoutput, minihalfadder_12_dataoutput,
       minihalfadder_13_dataoutput, minihalfadder_14_dataoutput, minihalfadder_15_dataoutput,
       minihalfadder_16_dataoutput;
  wire [15:0] multiplexer_1_out, register_1_q, reverse_1_dataoutput;

  minihalfadder minihalfadder_1 (
    .AInput(register_1_q[0]), .BInput(minihalfadder_2_dataoutput[0]), .DataOutput(minihalfadder_1_dataoutput));
  minihalfadder minihalfadder_2 (
    .AInput(register_1_q[1]), .BInput(minihalfadder_3_dataoutput[0]), .DataOutput(minihalfadder_2_dataoutput));
  minihalfadder minihalfadder_3 (
    .AInput(register_1_q[2]), .BInput(minihalfadder_4_dataoutput[0]), .DataOutput(minihalfadder_3_dataoutput));
  minihalfadder minihalfadder_4 (
    .AInput(register_1_q[3]), .BInput(minihalfadder_5_dataoutput[0]), .DataOutput(minihalfadder_4_dataoutput));
  minihalfadder minihalfadder_5 (
    .AInput(register_1_q[4]), .BInput(minihalfadder_6_dataoutput[0]), .DataOutput(minihalfadder_5_dataoutput));
  minihalfadder minihalfadder_6 (
    .AInput(register_1_q[5]), .BInput(minihalfadder_7_dataoutput[0]), .DataOutput(minihalfadder_6_dataoutput));
  minihalfadder minihalfadder_7 (
    .AInput(register_1_q[6]), .BInput(minihalfadder_8_dataoutput[0]), .DataOutput(minihalfadder_7_dataoutput));
  minihalfadder minihalfadder_8 (
    .AInput(register_1_q[7]), .BInput(minihalfadder_9_dataoutput[0]), .DataOutput(minihalfadder_8_dataoutput));
  minihalfadder minihalfadder_9 (
    .AInput(register_1_q[8]), .BInput(minihalfadder_10_dataoutput[0]), .DataOutput(minihalfadder_9_dataoutput));
  minihalfadder minihalfadder_10 (
    .AInput(register_1_q[9]), .BInput(minihalfadder_11_dataoutput[0]),
    .DataOutput(minihalfadder_10_dataoutput));
  minihalfadder minihalfadder_11 (
    .AInput(register_1_q[10]), .BInput(minihalfadder_12_dataoutput[0]),
    .DataOutput(minihalfadder_11_dataoutput));
  minihalfadder minihalfadder_12 (
    .AInput(register_1_q[11]), .BInput(minihalfadder_13_dataoutput[0]),
    .DataOutput(minihalfadder_12_dataoutput));
  minihalfadder minihalfadder_13 (
    .AInput(register_1_q[12]), .BInput(minihalfadder_14_dataoutput[0]),
    .DataOutput(minihalfadder_13_dataoutput));
  minihalfadder minihalfadder_14 (
    .AInput(register_1_q[13]), .BInput(minihalfadder_15_dataoutput[0]),
    .DataOutput(minihalfadder_14_dataoutput));
  minihalfadder minihalfadder_15 (
    .AInput(register_1_q[14]), .BInput(minihalfadder_16_dataoutput[0]),
    .DataOutput(minihalfadder_15_dataoutput));
  minihalfadder minihalfadder_16 (.AInput(register_1_q[15]), .BInput(1'b1), .DataOutput(minihalfadder_16_dataoutput));
  not not_1 (not_1_out, DirectNumber);
  Register #(.width(16)) register_1 (.D(multiplexer_1_out), .en(1'b1), .clk(RunCycle), .Q(register_1_q), .clr(Reset));
  Multiplexer #(.width(16)) multiplexer_1 (
    .in0(reverse_1_dataoutput),
    .in1({minihalfadder_16_dataoutput[1], minihalfadder_15_dataoutput[1], minihalfadder_14_dataoutput[1], minihalfadder_13_dataoutput[1], minihalfadder_12_dataoutput[1], minihalfadder_11_dataoutput[1], minihalfadder_10_dataoutput[1], minihalfadder_9_dataoutput[1], minihalfadder_8_dataoutput[1], minihalfadder_7_dataoutput[1], minihalfadder_6_dataoutput[1], minihalfadder_5_dataoutput[1], minihalfadder_4_dataoutput[1], minihalfadder_3_dataoutput[1], minihalfadder_2_dataoutput[1], minihalfadder_1_dataoutput[1]}),
    .out(multiplexer_1_out), .sel(not_1_out));
  reverse reverse_1 (.DataInput(NumberInput), .DataOutput(reverse_1_dataoutput));
  reverse reverse_2 (.DataInput(register_1_q), .DataOutput(Counter));
endmodule

module registers (
  input  Clock,
  input  [15:0] WData,
  input  Reset,
  input  WE,
  input  [3:0] WAddr,
  input  [3:0] RAddrA,
  input  [3:0] RAddrB,
  output [15:0] AOutput,
  output [15:0] BOutput
);

  wire decoder_1_out0, decoder_1_out1, decoder_1_out2, decoder_1_out3, decoder_1_out4, decoder_1_out5,
       decoder_1_out6, decoder_1_out7, decoder_1_out8, decoder_1_out9, decoder_1_out10, decoder_1_out11,
       decoder_1_out12, decoder_1_out13, decoder_1_out14, decoder_1_out15;
  wire [15:0] R0, R1, R2, R3, R4, R5, R6, R7, R8, R9, R10, R11, R12, R13, R14, R15;

  Decoder #(.select(4)) decoder_1 (
    .out0(decoder_1_out0), .out1(decoder_1_out1), .out2(decoder_1_out2), .out3(decoder_1_out3),
    .out4(decoder_1_out4), .out5(decoder_1_out5), .out6(decoder_1_out6), .out7(decoder_1_out7),
    .out8(decoder_1_out8), .out9(decoder_1_out9), .out10(decoder_1_out10), .out11(decoder_1_out11),
    .out12(decoder_1_out12), .out13(decoder_1_out13), .out14(decoder_1_out14), .out15(decoder_1_out15),
    .sel(WAddr), .en(WE));
  Register #(.width(16)) register_1 (.D(WData), .en(decoder_1_out0), .clk(Clock), .Q(R0), .clr(Reset));
  Register #(.width(16)) register_2 (.D(WData), .en(decoder_1_out1), .clk(Clock), .Q(R1), .clr(Reset));
  Register #(.width(16)) register_3 (.D(WData), .en(decoder_1_out2), .clk(Clock), .Q(R2), .clr(Reset));
  Register #(.width(16)) register_4 (.D(WData), .en(decoder_1_out3), .clk(Clock), .Q(R3), .clr(Reset));
  Register #(.width(16)) register_5 (.D(WData), .en(decoder_1_out4), .clk(Clock), .Q(R4), .clr(Reset));
  Register #(.width(16)) register_6 (.D(WData), .en(decoder_1_out5), .clk(Clock), .Q(R5), .clr(Reset));
  Register #(.width(16)) register_7 (.D(WData), .en(decoder_1_out6), .clk(Clock), .Q(R6), .clr(Reset));
  Register #(.width(16)) register_8 (.D(WData), .en(decoder_1_out7), .clk(Clock), .Q(R7), .clr(Reset));
  Register #(.width(16)) register_9 (.D(WData), .en(decoder_1_out8), .clk(Clock), .Q(R8), .clr(Reset));
  Register #(.width(16)) register_10 (.D(WData), .en(decoder_1_out9), .clk(Clock), .Q(R9), .clr(Reset));
  Register #(.width(16)) register_11 (.D(WData), .en(decoder_1_out10), .clk(Clock), .Q(R10), .clr(Reset));
  Register #(.width(16)) register_12 (.D(WData), .en(decoder_1_out11), .clk(Clock), .Q(R11), .clr(Reset));
  Register #(.width(16)) register_13 (.D(WData), .en(decoder_1_out12), .clk(Clock), .Q(R12), .clr(Reset));
  Register #(.width(16)) register_14 (.D(WData), .en(decoder_1_out13), .clk(Clock), .Q(R13), .clr(Reset));
  Register #(.width(16)) register_15 (.D(WData), .en(decoder_1_out14), .clk(Clock), .Q(R14), .clr(Reset));
  Register #(.width(16)) register_16 (.D(WData), .en(decoder_1_out15), .clk(Clock), .Q(R15), .clr(Reset));
  Multiplexer #(.select(4), .width(16)) multiplexer_1 (
    .in0(R0), .in1(R1), .in2(R2), .in3(R3), .in4(R4), .in5(R5), .in6(R6), .in7(R7), .in8(R8), .in9(R9),
    .in10(R10), .in11(R11), .in12(R12), .in13(R13), .in14(R14), .in15(R15), .out(AOutput), .sel(RAddrA));
  Multiplexer #(.select(4), .width(16)) multiplexer_2 (
    .in0(R0), .in1(R1), .in2(R2), .in3(R3), .in4(R4), .in5(R5), .in6(R6), .in7(R7), .in8(R8), .in9(R9),
    .in10(R10), .in11(R11), .in12(R12), .in13(R13), .in14(R14), .in15(R15), .out(BOutput), .sel(RAddrB));
endmodule

module adaptedALU (
  input  Cin,
  input  [15:0] AInput,
  input  [15:0] BInput,
  input  [3:0] ControlInput,
  input  Clock,
  output [5:0] FlagsRegister,
  output [15:0] HighOutput,
  output [15:0] LowOutput
);

  wire button_1_out;
  wire [5:0] alu_1_flagsbus;
  wire [15:0] alu_1_highoutput, alu_1_lowoutput, reverse_1_dataoutput, reverse_2_dataoutput;

  reverse reverse_1 (.DataInput(AInput), .DataOutput(reverse_1_dataoutput));
  reverse reverse_2 (.DataInput(BInput), .DataOutput(reverse_2_dataoutput));
  ALU alu_1 (
    .AInput(reverse_1_dataoutput), .BInput(reverse_2_dataoutput), .Cin(Cin),
    .ControlInput({ControlInput[0], ControlInput[1], ControlInput[2], ControlInput[3]}),
    .HighOutput(alu_1_highoutput), .LowOutput(alu_1_lowoutput), .FlagsBus(alu_1_flagsbus));
  reverse reverse_3 (.DataInput(alu_1_highoutput), .DataOutput(HighOutput));
  reverse reverse_4 (.DataInput(alu_1_lowoutput), .DataOutput(LowOutput));
  Register #(.width(6)) register_1 (.D(alu_1_flagsbus), .en(1'b1), .clk(Clock), .Q(FlagsRegister), .clr(button_1_out));
  Button button_1 (.out(button_1_out));
endmodule
